// Logisim project Banco de dados.circ as structural Verilog: 2 circuits, main circuit main
module main (
  input  [7:0] Entradas,
  input  Clock,
  input  Clear,
  input  Enable,
  input  Preset,
  output [7:0] Saidas,
  output [7:0] Saidas_tilde
);

  D_Flip_Flop d_ff_1 (
    .clk(Clock), .D(Entradas[7]), .Q(Saidas[7]), .Qn(Saidas_tilde[7]), .preset(Preset), .en(Enable),
    .reset(Clear));
  D_Flip_Flop d_ff_2 (
    .clk(Clock), .D(Entradas[6]), .Q(Saidas[6]), .Qn(Saidas_tilde[6]), .preset(Preset), .en(Enable),
    .reset(Clear));
  D_Flip_Flop d_ff_3 (
    .clk(Clock), .D(Entradas[5]), .Q(Saidas[5]), .Qn(Saidas_tilde[5]), .preset(Preset), .en(Enable),
    .reset(Clear));
  D_Flip_Flop d_ff_4 (
    .clk(Clock), .D(Entradas[4]), .Q(Saidas[4]), .Qn(Saidas_tilde[4]), .preset(Preset), .en(Enable),
    .reset(Clear));
  D_Flip_Flop d_ff_5 (
    .clk(Clock), .D(Entradas[3]), .Q(Saidas[3]), .Qn(Saidas_tilde[3]), .preset(Preset), .en(Enable),
    .reset(Clear));
  D_Flip_Flop d_ff_6 (
    .clk(Clock), .D(Entradas[2]), .Q(Saidas[2]), .Qn(Saidas_tilde[2]), .preset(Preset), .en(Enable),
    .reset(Clear));
  D_Flip_Flop d_ff_7 (
    .clk(Clock), .D(Entradas[1]), .Q(Saidas[1]), .Qn(Saidas_tilde[1]), .preset(Preset), .en(Enable),
    .reset(Clear));
  D_Flip_Flop d_ff_8 (
    .clk(Clock), .D(Entradas[0]), .Q(Saidas[0]), .Qn(Saidas_tilde[0]), .preset(Preset), .en(Enable),
    .reset(Clear));

  // Notes on the sheet:
  //   Clear força o zero
  //   Enable abilita o clock
  //   Preset força o um
endmodule

module Banco_completo (
  input  Wreiter,
  input  [3:0] Seletor,
  input  [3:0] in_3,
  input  [7:0] Entradas,
  input  Clear,
  input  Enable,
  input  Preset,
  input  [3:0] Seletor_2,
  output [7:0] Saidas,
  output [7:0] Saidas_tilde
);

  wire demultiplexer_1_out0, demultiplexer_1_out1, demultiplexer_1_out2, demultiplexer_1_out3,
       demultiplexer_1_out4, demultiplexer_1_out5, demultiplexer_1_out6, demultiplexer_1_out7,
       demultiplexer_1_out8, demultiplexer_1_out9, demultiplexer_1_out10, demultiplexer_1_out11,
       demultiplexer_1_out12, demultiplexer_1_out13, demultiplexer_1_out14, demultiplexer_1_out15;
  wire [7:0] main_1_saidas, main_1_saidas_tilde, main_2_saidas, main_2_saidas_tilde, main_3_saidas,
       main_3_saidas_tilde, main_4_saidas, main_4_saidas_tilde, main_5_saidas, main_5_saidas_tilde,
       main_6_saidas, main_6_saidas_tilde, main_7_saidas, main_7_saidas_tilde, main_8_saidas,
       main_8_saidas_tilde, main_9_saidas, main_9_saidas_tilde, main_10_saidas, main_10_saidas_tilde,
       main_11_saidas, main_11_saidas_tilde, main_12_saidas, main_12_saidas_tilde, main_13_saidas,
       main_13_saidas_tilde, main_14_saidas, main_14_saidas_tilde, main_15_saidas, main_15_saidas_tilde,
       main_16_saidas, main_16_saidas_tilde;

  Demultiplexer #(.select(4)) demultiplexer_1 (
    .out0(demultiplexer_1_out0), .out1(demultiplexer_1_out1), .out2(demultiplexer_1_out2),
    .out3(demultiplexer_1_out3), .out4(demultiplexer_1_out4), .out5(demultiplexer_1_out5),
    .out6(demultiplexer_1_out6), .out7(demultiplexer_1_out7), .out8(demultiplexer_1_out8),
    .out9(demultiplexer_1_out9), .out10(demultiplexer_1_out10), .out11(demultiplexer_1_out11),
    .out12(demultiplexer_1_out12), .out13(demultiplexer_1_out13), .out14(demultiplexer_1_out14),
    .out15(demultiplexer_1_out15), .in(Wreiter), .sel(in_3));  // open: en
  main main_1 (
    .Entradas(Entradas), .Clock(demultiplexer_1_out15), .Clear(Clear), .Enable(Enable), .Preset(Preset),
    .Saidas(main_1_saidas), .Saidas_tilde(main_1_saidas_tilde));
  main main_2 (
    .Entradas(Entradas), .Clock(demultiplexer_1_out7), .Clear(Clear), .Enable(Enable), .Preset(Preset),
    .Saidas(main_2_saidas), .Saidas_tilde(main_2_saidas_tilde));
  main main_3 (
    .Entradas(Entradas), .Clock(demultiplexer_1_out14), .Clear(Clear), .Enable(Enable), .Preset(Preset),
    .Saidas(main_3_saidas), .Saidas_tilde(main_3_saidas_tilde));
  main main_4 (
    .Entradas(Entradas), .Clock(demultiplexer_1_out6), .Clear(Clear), .Enable(Enable), .Preset(Preset),
    .Saidas(main_4_saidas), .Saidas_tilde(main_4_saidas_tilde));
  main main_5 (
    .Entradas(Entradas), .Clock(demultiplexer_1_out13), .Clear(Clear), .Enable(Enable), .Preset(Preset),
    .Saidas(main_5_saidas), .Saidas_tilde(main_5_saidas_tilde));
  main main_6 (
    .Entradas(Entradas), .Clock(demultiplexer_1_out5), .Clear(Clear), .Enable(Enable), .Preset(Preset),
    .Saidas(main_6_saidas), .Saidas_tilde(main_6_saidas_tilde));
  main main_7 (
    .Entradas(Entradas), .Clock(demultiplexer_1_out12), .Clear(Clear), .Enable(Enable), .Preset(Preset),
    .Saidas(main_7_saidas), .Saidas_tilde(main_7_saidas_tilde));
  main main_8 (
    .Entradas(Entradas), .Clock(demultiplexer_1_out4), .Clear(Clear), .Enable(Enable), .Preset(Preset),
    .Saidas(main_8_saidas), .Saidas_tilde(main_8_saidas_tilde));
  main main_9 (
    .Entradas(Entradas), .Clock(demultiplexer_1_out11), .Clear(Clear), .Enable(Enable), .Preset(Preset),
    .Saidas(main_9_saidas), .Saidas_tilde(main_9_saidas_tilde));
  main main_10 (
    .Entradas(Entradas), .Clock(demultiplexer_1_out3), .Clear(Clear), .Enable(Enable), .Preset(Preset),
    .Saidas(main_10_saidas), .Saidas_tilde(main_10_saidas_tilde));
  main main_11 (
    .Entradas(Entradas), .Clock(demultiplexer_1_out10), .Clear(Clear), .Enable(Enable), .Preset(Preset),
    .Saidas(main_11_saidas), .Saidas_tilde(main_11_saidas_tilde));
  main main_12 (
    .Entradas(Entradas), .Clock(demultiplexer_1_out2), .Clear(Clear), .Enable(Enable), .Preset(Preset),
    .Saidas(main_12_saidas), .Saidas_tilde(main_12_saidas_tilde));
  main main_13 (
    .Entradas(Entradas), .Clock(demultiplexer_1_out9), .Clear(Clear), .Enable(Enable), .Preset(Preset),
    .Saidas(main_13_saidas), .Saidas_tilde(main_13_saidas_tilde));
  main main_14 (
    .Entradas(Entradas), .Clock(demultiplexer_1_out1), .Clear(Clear), .Enable(Enable), .Preset(Preset),
    .Saidas(main_14_saidas), .Saidas_tilde(main_14_saidas_tilde));
  main main_15 (
    .Entradas(Entradas), .Clock(demultiplexer_1_out8), .Clear(Clear), .Enable(Enable), .Preset(Preset),
    .Saidas(main_15_saidas), .Saidas_tilde(main_15_saidas_tilde));
  main main_16 (
    .Entradas(Entradas), .Clock(demultiplexer_1_out0), .Clear(Clear), .Enable(Enable), .Preset(Preset),
    .Saidas(main_16_saidas), .Saidas_tilde(main_16_saidas_tilde));
  Multiplexer #(.select(4), .width(8)) multiplexer_1 (
    .in0(main_16_saidas), .in1(main_14_saidas), .in2(main_12_saidas), .in3(main_10_saidas),
    .in4(main_8_saidas), .in5(main_6_saidas), .in6(main_4_saidas), .in7(main_2_saidas), .in8(main_15_saidas),
    .in9(main_13_saidas), .in10(main_11_saidas), .in11(main_9_saidas), .in12(main_7_saidas),
    .in13(main_5_saidas), .in14(main_3_saidas), .in15(main_1_saidas), .out(Saidas), .sel(Seletor));  // open: en
  Multiplexer #(.select(4), .width(8)) multiplexer_2 (
    .in0(main_16_saidas_tilde), .in1(main_14_saidas_tilde), .in2(main_12_saidas_tilde),
    .in3(main_10_saidas_tilde), .in4(main_8_saidas_tilde), .in5(main_6_saidas_tilde),
    .in6(main_4_saidas_tilde), .in7(main_2_saidas_tilde), .in8(main_15_saidas_tilde),
    .in9(main_13_saidas_tilde), .in10(main_11_saidas_tilde), .in11(main_9_saidas_tilde),
    .in12(main_7_saidas_tilde), .in13(main_5_saidas_tilde), .in14(main_3_saidas_tilde),
    .in15(main_1_saidas_tilde), .out(Saidas_tilde), .sel(Seletor_2));  // open: en
endmodule
